# Fritzing sketch PETITBOT_avec_sonar_simple (saved by Fritzing 0.9.3b)
breadboards: 1

parts:
  hc-sr1 = hc-sr04
  WeMos_D1_Mini1 = WeMos D1 Mini
  VCC1 = 4 x AAA Battery Mount
  J2 = Basic Servo
  J1 = Basic Servo

nets:
  VCC: hc-sr1.VCC, WeMos_D1_Mini1.5V, VCC1.+, J2.vcc, J1.vcc
  N1: hc-sr1.Trig, WeMos_D1_Mini1.D5
  N2: hc-sr1.Echo, WeMos_D1_Mini1.D0
  GND: hc-sr1.GND, WeMos_D1_Mini1.G, VCC1.-, J2.gnd, J1.gnd
  N3: WeMos_D1_Mini1.D1, J1.pulse
  N4: WeMos_D1_Mini1.D2, J2.pulse
